# Fritzing sketch Untitled Sketch (saved by Fritzing 0.9.5d)
breadboards: 1

parts:
  Mod1 = Raspberry Pi Pico W
  WATER_PUMP1 = water pump/motor
  Chirp!_Soil_Moisture_Sensor1 = Chirp! Soil Moisture Sensor v2.7.3
  J1 = Dagu DGServo 9g header connector (female) [package=THT]

nets:
  N1: Mod1.pin_1, WATER_PUMP1.pin_2
  N2: Mod1.pin_2, J1.gnd
  N3: Mod1.pin_3, Mod1.pin_8, Mod1.pin_13, Mod1.pin_18, Mod1.pin_23, Mod1.pin_28, Mod1.pin_33, Mod1.pin_38, WATER_PUMP1.pin_1, Chirp!_Soil_Moisture_Sensor1.pin_5, J1.pulse
  N4: Mod1.pin_31, Chirp!_Soil_Moisture_Sensor1.pin_3
  N5: Mod1.pin_40, Chirp!_Soil_Moisture_Sensor1.Pin_1, J1.Vcc

custom parts:
  Raspberry Pi Pico W: Raspberry Pi Pico W. Based around the RP2040 microcontroller the Pico W is a low cost microcontroller device bringing Raspberry Pi quality, cost, and easy of use to the microcontroller space. The areas marked KEEPOUT in pcb silkscreen should not have traces running through them to avoid shorts on a soldered in module!
  water pump/motor: WATER PUMP BY ARDUBLOCKTR
